// Logisim project MUX4B.circ as structural Verilog: 2 circuits, main circuit main
module main (
  input  [3:0] in_1,
  input  [3:0] in_2,
  input  in_3,
  output [3:0] out_4
);

  // MUX4B mux4b_1: pin names not known; wires that end beside it: out_4, in_2, in_3
endmodule

module MUX4B (
  input  in_1,
  input  in_2,
  input  in_3,
  input  in_4,
  input  in_5,
  input  in_6,
  input  in_7,
  input  in_8,
  input  in_9,
  output out_10,
  output out_11,
  output out_12,
  output out_13
);

  Multiplexer #(.enable("false")) multiplexer_1 (.in0(in_1), .in1(in_5), .out(out_10), .sel(in_9));
  Multiplexer #(.enable("false")) multiplexer_2 (.in0(in_2), .in1(in_6), .out(out_11), .sel(in_9));
  Multiplexer #(.enable("false")) multiplexer_3 (.in0(in_3), .in1(in_7), .out(out_12), .sel(in_9));
  Multiplexer #(.enable("false")) multiplexer_4 (.in0(in_4), .in1(in_8), .out(out_13), .sel(in_9));

  // Notes on the sheet:
  //   lucas lopes arantes
endmodule
