// Logisim project REGISTRADOR.circ as structural Verilog: 7 circuits, main circuit main
module main (
  input  in_1,
  input  [1:0] Decod_C,
  input  [1:0] Decod_A,
  input  [1:0] Decod_B,
  input  [1:0] in_5,
  input  [3:0] in_6,
  output out_7,
  output out_8,
  output [3:0] out_9
);

  wire clock_1_out;
  wire [3:0] registradores_1_out_7, registradores_1_out_8;

  Clock clock_1 (.out(clock_1_out));
  registradores registradores_1 (
    .CK(clock_1_out), .C(Decod_C), .in_5(in_6), .out_7(registradores_1_out_7), .out_8(registradores_1_out_8),
    .A(Decod_A), .B(Decod_B), .ValC(in_1));
  ULA4B ula4b_1 (
    .A(registradores_1_out_7), .in_2(registradores_1_out_8), .Select(in_5), .out_6(out_9), .Sinal(out_8),
    .Z(out_7));
endmodule

// REG4B
module reg4b (
  input  CK,
  input  [3:0] DADOS,
  input  OE1_prime,
  input  OE2_prime,
  output [3:0] saida_A,
  output [3:0] saida_B
);

  wire not_1_out, not_2_out;
  wire [3:0] d_ff_4_q;

  D_Flip_Flop #(.trigger("falling")) d_ff_1 (.clk(CK), .D(DADOS[3]), .Q(d_ff_4_q[3]));  // open: Qn, preset, reset
  D_Flip_Flop #(.trigger("falling")) d_ff_2 (.clk(CK), .D(DADOS[2]), .Q(d_ff_4_q[2]));  // open: Qn, preset, reset
  D_Flip_Flop #(.trigger("falling")) d_ff_3 (.clk(CK), .D(DADOS[1]), .Q(d_ff_4_q[1]));  // open: Qn, preset, reset
  D_Flip_Flop #(.trigger("falling")) d_ff_4 (.clk(CK), .D(DADOS[0]), .Q(d_ff_4_q[0]));  // open: Qn, preset, reset
  not not_1 (not_1_out, OE1_prime);
  not not_2 (not_2_out, OE2_prime);
  assign saida_A = not_1_out ? d_ff_4_q : 4'bz;  // Controlled_Buffer controlled_buffer_1
  assign saida_B = not_2_out ? d_ff_4_q : 4'bz;  // Controlled_Buffer controlled_buffer_2
endmodule

// REGS
module registradores (
  input  ValC,
  input  CK,
  input  [1:0] C,
  input  [1:0] A,
  input  [3:0] in_5,
  input  [1:0] B,
  output [3:0] out_7,
  output [3:0] out_8
);

  wire decod2_1_out_2, decod2_1_out_3, decod2_1_out_4, decod2_1_out_5, decod2_2_out_2, decod2_2_out_3,
       decod2_2_out_4, decod2_2_out_5, decod_1_out_4, decod_1_out_5, decod_1_out_6, decod_1_out_7;

  decod decod_1 (
    .in_2(CK), .in_3(C), .out_4(decod_1_out_4), .out_5(decod_1_out_5), .out_6(decod_1_out_6),
    .out_7(decod_1_out_7), .in_1(ValC));
  decod2 decod2_1 (
    .in_1(A), .out_2(decod2_1_out_2), .out_3(decod2_1_out_3), .out_4(decod2_1_out_4), .out_5(decod2_1_out_5));
  decod2 decod2_2 (
    .in_1(B), .out_2(decod2_2_out_2), .out_3(decod2_2_out_3), .out_4(decod2_2_out_4), .out_5(decod2_2_out_5));
  reg4b reg4b_1 (
    .CK(decod_1_out_4), .DADOS(in_5), .OE1_prime(decod2_1_out_2), .OE2_prime(decod2_2_out_2),
    .saida_A(out_7), .saida_B(out_8));
  reg4b reg4b_2 (
    .CK(decod_1_out_5), .DADOS(in_5), .OE1_prime(decod2_1_out_3), .OE2_prime(decod2_2_out_3),
    .saida_A(out_7), .saida_B(out_8));
  reg4b reg4b_3 (
    .CK(decod_1_out_6), .DADOS(in_5), .OE1_prime(decod2_1_out_4), .OE2_prime(decod2_2_out_4),
    .saida_A(out_7), .saida_B(out_8));
  reg4b reg4b_4 (
    .CK(decod_1_out_7), .DADOS(in_5), .OE1_prime(decod2_1_out_5), .OE2_prime(decod2_2_out_5),
    .saida_A(out_7), .saida_B(out_8));
endmodule

// DC
module decod (
  input  in_1,
  input  in_2,
  input  [1:0] in_3,
  output out_4,
  output out_5,
  output out_6,
  output out_7
);

  wire and_1_out, decoder_1_out0, decoder_1_out1, decoder_1_out2, decoder_1_out3;

  Decoder #(.select(2), .enable("false")) decoder_1 (
    .out0(decoder_1_out0), .out1(decoder_1_out1), .out2(decoder_1_out2), .out3(decoder_1_out3), .sel(in_3));
  and and_1 (and_1_out, in_1, in_2);
  and and_2 (out_4, and_1_out, decoder_1_out0);
  and and_3 (out_5, and_1_out, decoder_1_out1);
  and and_4 (out_6, and_1_out, decoder_1_out2);
  and and_5 (out_7, and_1_out, decoder_1_out3);
endmodule

module decod2 (
  input  [1:0] in_1,
  output out_2,
  output out_3,
  output out_4,
  output out_5
);

  wire decoder_1_out0, decoder_1_out1, decoder_1_out2, decoder_1_out3;

  Decoder #(.select(2), .enable("false")) decoder_1 (
    .out0(decoder_1_out0), .out1(decoder_1_out1), .out2(decoder_1_out2), .out3(decoder_1_out3), .sel(in_1));
  not not_1 (out_2, decoder_1_out0);
  not not_2 (out_3, decoder_1_out1);
  not not_3 (out_4, decoder_1_out2);
  not not_4 (out_5, decoder_1_out3);
endmodule

module ULA1B (
  input  A,
  input  B,
  input  Te,
  input  [1:0] S1_S0,
  output Ts,
  output out_6
);

  wire and_1_out, and_2_out, and_3_out, and_4_out, not_1_out, xor_1_out, xor_2_out;

  xor xor_1 (xor_1_out, A, B);
  and and_1 (and_1_out, A, Te);
  and and_2 (and_2_out, B, Te);
  and and_3 (and_3_out, A, B);
  and and_4 (and_4_out, A, B);
  not not_1 (not_1_out, A);
  xor xor_2 (xor_2_out, xor_1_out, Te);
  or or_1 (Ts, and_1_out, and_2_out, and_3_out);
  Multiplexer #(.select(2), .enable("false")) multiplexer_1 (
    .in0(xor_2_out), .in1(and_4_out), .in2(A), .in3(not_1_out), .out(out_6), .sel(S1_S0));

  // Notes on the sheet:
  //   ATe
  //   BTe
  //   AB
  //   And
  //   A
  //   A\
  //   soma
  //   Ts
endmodule

module ULA4B (
  input  [3:0] A,
  input  [3:0] in_2,
  input  [1:0] Select,
  output Sinal,
  output Z,
  output [3:0] out_6
);

  wire or_1_out, ula1b_2_ts, ula1b_3_ts, ula1b_4_ts;

  not not_1 (Z, or_1_out);
  ULA1B ula1b_1 (.out_6(out_6[3]), .A(A[3]), .B(in_2[3]), .Te(ula1b_2_ts), .S1_S0(Select));  // open: Ts
  or or_1 (or_1_out, out_6[3], out_6[2], out_6[1], out_6[0]);
  ULA1B ula1b_2 (.out_6(out_6[2]), .A(A[2]), .B(in_2[2]), .Te(ula1b_3_ts), .Ts(ula1b_2_ts), .S1_S0(Select));
  ULA1B ula1b_3 (.out_6(out_6[1]), .A(A[1]), .B(in_2[1]), .Te(ula1b_4_ts), .Ts(ula1b_3_ts), .S1_S0(Select));
  ULA1B ula1b_4 (.out_6(out_6[0]), .A(A[0]), .B(in_2[0]), .Te(1'b0), .Ts(ula1b_4_ts), .S1_S0(Select));

  assign Sinal = out_6[3];
endmodule
